// Logisim project G5_DSDProject_Completed.circ as structural Verilog: 19 circuits, main circuit main
module main (
  input  E,
  input  X,
  input  R
);

  wire clock_1_out, leselector_1_green, leselector_1_red, leselector_1_yellow, lxselector_1_green,
       lxselector_1_red, lxselector_1_yellow, sevensegment_1_a, sevensegment_1_b, sevensegment_1_c,
       sevensegment_1_d, sevensegment_1_e, sevensegment_1_f, sevensegment_1_g, trafficcontroller_1_out_5,
       trafficcontroller_1_out_6, trafficcontroller_1_out_7, trafficcontroller_1_out_8,
       trafficcontroller_1_out_9, trafficcontroller_1_out_10, trafficcontroller_1_out_11,
       trafficcontroller_1_out_12;

  Clock clock_1 (.out(clock_1_out));
  TrafficController trafficcontroller_1 (
    .E(E), .X(X), .CLK(clock_1_out), .Reset(R), .out_5(trafficcontroller_1_out_5),
    .out_6(trafficcontroller_1_out_6), .out_7(trafficcontroller_1_out_7), .out_8(trafficcontroller_1_out_8),
    .out_9(trafficcontroller_1_out_9), .out_10(trafficcontroller_1_out_10),
    .out_11(trafficcontroller_1_out_11), .out_12(trafficcontroller_1_out_12));
  LED led_1 (.in(leselector_1_red));
  LESelector leselector_1 (
    .LE0(trafficcontroller_1_out_5), .LE1(trafficcontroller_1_out_6), .Red(leselector_1_red),
    .Yellow(leselector_1_yellow), .Green(leselector_1_green));
  LED led_2 (.in(leselector_1_yellow));
  LED led_3 (.in(leselector_1_green));
  LED led_4 (.in(lxselector_1_red));
  LXSelector lxselector_1 (
    .LX0(trafficcontroller_1_out_7), .LX1(trafficcontroller_1_out_8), .Red(lxselector_1_red),
    .Yellow(lxselector_1_yellow), .Green(lxselector_1_green));
  LED led_5 (.in(lxselector_1_yellow));
  LED led_6 (.in(lxselector_1_green));
  SevenSegment sevensegment_1 (
    .C0(trafficcontroller_1_out_12), .C1(trafficcontroller_1_out_11), .C2(trafficcontroller_1_out_10),
    .C3(trafficcontroller_1_out_9), .A(sevensegment_1_a), .B(sevensegment_1_b), .C(sevensegment_1_c),
    .D(sevensegment_1_d), .E(sevensegment_1_e), .F(sevensegment_1_f), .G(sevensegment_1_g));
  _7_Segment_Display u_7_segment_display_1 (
    .g(sevensegment_1_g), .f(sevensegment_1_f), .a(sevensegment_1_a), .b(sevensegment_1_b),
    .e(sevensegment_1_e), .d(sevensegment_1_d), .c(sevensegment_1_c));  // open: dp
endmodule

module TrafficController (
  input  E,
  input  X,
  input  CLK,
  input  Reset,
  output out_5,
  output out_6,
  output out_7,
  output out_8,
  output out_9,
  output out_10,
  output out_11,
  output out_12
);

  wire and_1_out, and_2_out, and_3_out, and_4_out, and_5_out, and_6_out, and_7_out, and_8_out, and_9_out,
       and_10_out, and_11_out, and_12_out, and_13_out, and_14_out, and_15_out, and_16_out, and_17_out,
       and_18_out, and_19_out, and_20_out, and_21_out, and_22_out, and_23_out, and_24_out, and_25_out,
       and_26_out, and_27_out, and_28_out, and_29_out, and_30_out, and_31_out, and_32_out, and_33_out,
       and_34_out, and_35_out, and_36_out, and_37_out, and_38_out, and_39_out, and_40_out, and_41_out,
       and_42_out, and_43_out, and_44_out, and_45_out, and_46_out, and_47_out, and_48_out, and_49_out,
       and_50_out, and_51_out, and_52_out, and_53_out, and_54_out, and_55_out, and_56_out, and_57_out,
       and_58_out, and_59_out, and_60_out, and_61_out, and_62_out, and_63_out, and_64_out, and_65_out,
       and_66_out, and_67_out, and_68_out, and_69_out, and_70_out, and_71_out, and_72_out, not_1_out,
       not_2_out, not_3_out, not_4_out, not_5_out, not_6_out, not_7_out, not_8_out;
  wire [5:0] or_1_out, register_1_q;

  not not_1 (not_1_out, register_1_q[0]);
  not not_2 (not_2_out, register_1_q[1]);
  not not_3 (not_3_out, register_1_q[2]);
  not not_4 (not_4_out, register_1_q[3]);
  not not_5 (not_5_out, register_1_q[4]);
  not not_6 (not_6_out, register_1_q[5]);
  not not_7 (not_7_out, E);
  not not_8 (not_8_out, X);
  and and_1 (and_1_out, register_1_q[0], not_5_out, not_8_out);
  and and_2 (and_2_out, register_1_q[0], register_1_q[5]);
  and and_3 (and_3_out, register_1_q[0], register_1_q[3], not_5_out);
  and and_4 (and_4_out, not_2_out, not_3_out, register_1_q[3], register_1_q[4], register_1_q[5], X);
  and and_5 (and_5_out, not_2_out, register_1_q[2], not_4_out, not_5_out, X);
  and and_6 (and_6_out, not_2_out, register_1_q[2], not_4_out, not_5_out, register_1_q[5]);
  and and_7 (and_7_out, register_1_q[1], register_1_q[2], register_1_q[3], register_1_q[4], register_1_q[5]);
  and and_8 (and_8_out, register_1_q[0], not_3_out, not_4_out, not_5_out, not_6_out, X);
  and and_9 (and_9_out, not_1_out, not_3_out, not_4_out, register_1_q[4], register_1_q[5], X);
  and and_10 (and_10_out, not_1_out, not_3_out, register_1_q[3], not_5_out, X);
  and and_11 (and_11_out, not_1_out, not_2_out, not_3_out, register_1_q[3], not_6_out, X);
  and and_12 (and_12_out, not_2_out, register_1_q[2], register_1_q[3], register_1_q[4], register_1_q[5]);
  and and_13 (and_13_out, register_1_q[1], not_5_out, not_8_out);
  and and_14 (and_14_out, register_1_q[1], not_3_out, register_1_q[5]);
  and and_15 (and_15_out, register_1_q[1], register_1_q[2], not_5_out);
  and and_16 (and_16_out, register_1_q[1], not_4_out, register_1_q[5]);
  and and_17 (and_17_out, register_1_q[0], not_3_out, not_4_out, not_5_out, not_6_out, X);
  and and_18 (and_18_out, not_1_out, not_2_out, not_5_out, register_1_q[5], X);
  and and_19 (and_19_out, not_1_out, not_2_out, not_3_out, register_1_q[4], not_6_out, X);
  and and_20 (and_20_out, register_1_q[0], register_1_q[3], register_1_q[4], E);
  and and_21 (and_21_out, register_1_q[0], register_1_q[3], register_1_q[4], register_1_q[5]);
  and and_22 (and_22_out, not_3_out, register_1_q[3], register_1_q[4], register_1_q[5], E, not_8_out);
  and and_23 (and_23_out, register_1_q[2], not_5_out, not_8_out);
  and and_24 (and_24_out, register_1_q[0], register_1_q[2], register_1_q[4]);
  and and_25 (and_25_out, register_1_q[2], not_4_out, register_1_q[5]);
  and and_26 (and_26_out, register_1_q[2], register_1_q[3], not_5_out);
  and and_27 (and_27_out, register_1_q[1], not_3_out, not_4_out, not_5_out, not_6_out, X);
  and and_28 (and_28_out, register_1_q[1], not_3_out, register_1_q[3], register_1_q[4], register_1_q[5]);
  and and_29 (and_29_out, register_1_q[0], not_3_out, not_4_out, register_1_q[4]);
  and and_30 (and_30_out, not_4_out, register_1_q[4], register_1_q[5], E, not_8_out);
  and and_31 (and_31_out, not_1_out, not_2_out, not_3_out, register_1_q[3], not_6_out);
  and and_32 (and_32_out, register_1_q[3], not_5_out, not_8_out);
  and and_33 (and_33_out, register_1_q[0], register_1_q[3], not_5_out, register_1_q[5]);
  and and_34 (and_34_out, not_1_out, not_2_out, not_3_out, register_1_q[3], not_7_out, not_8_out);
  and and_35 (and_35_out, register_1_q[2], not_4_out, not_5_out, not_6_out, X);
  and and_36 (and_36_out, register_1_q[2], not_4_out, register_1_q[4], register_1_q[5]);
  and and_37 (and_37_out, register_1_q[2], register_1_q[3], not_5_out, register_1_q[5]);
  and and_38 (and_38_out, register_1_q[1], not_4_out, not_5_out, not_6_out, X);
  and and_39 (and_39_out, register_1_q[1], not_4_out, register_1_q[4], register_1_q[5]);
  and and_40 (and_40_out, register_1_q[1], register_1_q[3], not_5_out, register_1_q[5]);
  and and_41 (and_41_out, register_1_q[1], register_1_q[2], register_1_q[4], not_6_out);
  and and_42 (and_42_out, register_1_q[0], not_3_out, register_1_q[4], not_6_out, not_7_out);
  and and_43 (and_43_out, register_1_q[0], not_3_out, not_4_out, not_6_out, X);
  and and_44 (and_44_out, not_1_out, not_2_out, not_3_out, register_1_q[4], not_6_out, X);
  and and_45 (and_45_out, register_1_q[1], register_1_q[3], register_1_q[4], not_6_out, E);
  and and_46 (and_46_out, register_1_q[0], not_5_out, register_1_q[5]);
  and and_47 (and_47_out, not_5_out, register_1_q[5], E);
  and and_48 (and_48_out, not_3_out, not_4_out, register_1_q[4], not_6_out);
  and and_49 (and_49_out, not_1_out, not_2_out, not_3_out, register_1_q[4], not_7_out);
  and and_50 (and_50_out, not_1_out, not_2_out, register_1_q[2], not_5_out, X);
  and and_51 (and_51_out, register_1_q[2], not_5_out, register_1_q[5]);
  and and_52 (and_52_out, register_1_q[1], not_5_out, register_1_q[5]);
  and and_53 (and_53_out, not_3_out, register_1_q[4], not_6_out, not_7_out);
  and and_54 (and_54_out, register_1_q[2], register_1_q[3], register_1_q[4], not_6_out, E);
  and and_55 (and_55_out, not_1_out, not_2_out, not_3_out, register_1_q[5], X);
  and and_56 (and_56_out, not_1_out, not_2_out, not_3_out, register_1_q[3], X);
  and and_57 (and_57_out, not_1_out, not_2_out, not_3_out, register_1_q[4], not_6_out);
  and and_58 (and_58_out, not_1_out, not_2_out, not_3_out, register_1_q[4], X);
  and and_59 (and_59_out, not_1_out, not_2_out, not_3_out, register_1_q[5], not_7_out);
  and and_60 (and_60_out, not_1_out, not_2_out, not_3_out, register_1_q[3], X);
  and and_61 (and_61_out, not_3_out, not_5_out, not_6_out, E, not_8_out);
  and and_62 (and_62_out, register_1_q[0], register_1_q[3], register_1_q[4], not_6_out, not_7_out);
  and and_63 (and_63_out, not_1_out, not_2_out, not_3_out, not_6_out, E);
  and and_64 (and_64_out, not_1_out, not_2_out, register_1_q[2], not_4_out, not_5_out, X);
  and and_65 (and_65_out, not_1_out, not_5_out, not_6_out, E, not_8_out);
  and and_66 (and_66_out, register_1_q[2], register_1_q[3], register_1_q[4], not_6_out, not_7_out);
  and and_67 (and_67_out, register_1_q[1], register_1_q[3], register_1_q[4], not_6_out, not_7_out);
  and and_68 (and_68_out, register_1_q[1], not_4_out, register_1_q[4], not_6_out, E);
  and and_69 (and_69_out, register_1_q[0], not_4_out, register_1_q[4], not_6_out, E);
  and and_70 (and_70_out, register_1_q[0], not_4_out, not_6_out, E, not_8_out);
  and and_71 (and_71_out, not_1_out, not_2_out, register_1_q[2], not_4_out, not_5_out, register_1_q[5]);
  and and_72 (and_72_out, not_1_out, not_2_out, not_3_out, E, X);
  or or_1 (or_1_out[0], and_1_out, and_2_out, and_3_out, and_4_out, and_5_out, and_6_out, and_7_out);
  or or_2 (or_1_out[1], and_8_out, and_9_out, and_10_out, and_11_out, and_12_out, and_13_out, and_14_out, and_15_out, and_16_out);
  or or_3 (or_1_out[2], and_17_out, and_18_out, and_19_out, and_20_out, and_21_out, and_22_out, and_23_out, and_24_out, and_25_out, and_26_out, and_27_out, and_28_out);
  or or_4 (or_1_out[3], and_29_out, and_30_out, and_31_out, and_32_out, and_33_out, and_34_out, and_35_out, and_36_out, and_37_out, and_38_out, and_39_out, and_40_out, and_41_out, and_42_out, and_43_out, and_44_out, and_45_out);
  or or_5 (or_1_out[4], and_46_out, and_47_out, and_48_out, and_49_out, and_50_out, and_51_out, and_52_out, and_53_out, and_54_out, and_55_out, and_56_out, and_57_out);
  or or_6 (or_1_out[5], and_58_out, and_59_out, and_60_out, and_61_out, and_62_out, and_63_out, and_64_out, and_65_out, and_66_out, and_67_out, and_68_out, and_69_out, and_70_out, and_71_out, and_72_out);
  Register #(.width(6)) register_1 (.D(or_1_out), .clk(CLK), .Q(register_1_q), .clr(Reset));  // open: en
  LE_0 le_0_1 (
    .s0(register_1_q[0]), .s1(register_1_q[1]), .s2(register_1_q[2]), .s3(register_1_q[3]),
    .s4(register_1_q[4]), .s5(register_1_q[5]), .O(out_5));
  LE_1 le_1_1 (
    .s0(register_1_q[0]), .s1(register_1_q[1]), .s2(register_1_q[2]), .s3(register_1_q[3]),
    .s4(register_1_q[4]), .s5(register_1_q[5]), .O(out_6));
  LX_0 lx_0_1 (
    .s0(register_1_q[0]), .s1(register_1_q[1]), .s2(register_1_q[2]), .s3(register_1_q[3]),
    .s4(register_1_q[4]), .s5(register_1_q[5]), .O(out_7));
  LX_1 lx_1_1 (
    .s0(register_1_q[0]), .s1(register_1_q[1]), .s2(register_1_q[2]), .s3(register_1_q[3]),
    .s4(register_1_q[4]), .s5(register_1_q[5]), .O(out_8));
  C_0 c_0_1 (
    .s0(register_1_q[0]), .s1(register_1_q[1]), .s2(register_1_q[2]), .s3(register_1_q[3]),
    .s4(register_1_q[4]), .s5(register_1_q[5]), .O(out_9));
  C_1 c_1_1 (
    .s0(register_1_q[0]), .s1(register_1_q[1]), .s2(register_1_q[2]), .s3(register_1_q[3]),
    .s4(register_1_q[4]), .s5(register_1_q[5]), .O(out_10));
  C_2 c_2_1 (
    .s0(register_1_q[0]), .s1(register_1_q[1]), .s2(register_1_q[2]), .s3(register_1_q[3]),
    .s4(register_1_q[4]), .s5(register_1_q[5]), .O(out_11));
  C_3 c_3_1 (
    .s0(register_1_q[0]), .s1(register_1_q[1]), .s2(register_1_q[2]), .s3(register_1_q[3]),
    .s4(register_1_q[4]), .s5(register_1_q[5]), .O(out_12));
endmodule

module SevenSegment (
  input  C0,
  input  C1,
  input  C2,
  input  C3,
  output A,
  output B,
  output C,
  output D,
  output E,
  output F,
  output G
);

  wire and_1_out, and_2_out, and_3_out, and_4_out, and_5_out, and_6_out, and_7_out, and_8_out, and_9_out,
       and_10_out, and_11_out, and_12_out, and_13_out, and_14_out, and_15_out, and_16_out, and_17_out,
       and_18_out, and_19_out, and_20_out, and_21_out, and_22_out, and_23_out, and_24_out, and_25_out,
       and_26_out, not_1_out, not_2_out, not_3_out, not_4_out;

  not not_1 (not_1_out, C3);
  not not_2 (not_2_out, C2);
  not not_3 (not_3_out, C1);
  not not_4 (not_4_out, C0);
  and and_1 (and_1_out, not_1_out, C1);
  and and_2 (and_2_out, not_1_out, C2, C0);
  and and_3 (and_3_out, C3, not_2_out, not_3_out);
  and and_4 (and_4_out, not_2_out, not_3_out, not_4_out);
  and and_5 (and_5_out, not_1_out, not_2_out);
  and and_6 (and_6_out, not_2_out, not_3_out);
  and and_7 (and_7_out, not_1_out, C1, C0);
  and and_8 (and_8_out, not_1_out, not_3_out, not_4_out);
  and and_9 (and_9_out, not_2_out, not_3_out);
  and and_10 (and_10_out, not_1_out, C2);
  and and_11 (and_11_out, not_1_out, C0);
  and and_12 (and_12_out, not_2_out, not_3_out, not_4_out);
  and and_13 (and_13_out, not_1_out, not_2_out, C1);
  and and_14 (and_14_out, not_1_out, C1, not_4_out);
  and and_15 (and_15_out, C3, not_2_out, not_3_out);
  and and_16 (and_16_out, not_1_out, C2, not_3_out, C0);
  and and_17 (and_17_out, not_2_out, not_3_out, not_4_out);
  and and_18 (and_18_out, not_1_out, C1, not_4_out);
  and and_19 (and_19_out, not_2_out, not_3_out, not_4_out);
  and and_20 (and_20_out, not_1_out, C2, not_3_out);
  and and_21 (and_21_out, not_1_out, C2, not_4_out);
  and and_22 (and_22_out, C3, not_2_out, not_3_out);
  and and_23 (and_23_out, not_1_out, not_2_out, C1);
  and and_24 (and_24_out, not_1_out, C2, not_3_out);
  and and_25 (and_25_out, not_1_out, C1, not_4_out);
  and and_26 (and_26_out, C3, not_2_out, not_3_out);
  or or_1 (A, and_1_out, and_2_out, and_3_out, and_4_out);
  or or_2 (B, and_5_out, and_6_out, and_7_out, and_8_out);
  or or_3 (C, and_9_out, and_10_out, and_11_out);
  or or_4 (D, and_12_out, and_13_out, and_14_out, and_15_out, and_16_out);
  or or_5 (E, and_17_out, and_18_out);
  or or_6 (F, and_19_out, and_20_out, and_21_out, and_22_out);
  or or_7 (G, and_23_out, and_24_out, and_25_out, and_26_out);
endmodule

module s0_Circuit (
  input  s0,
  input  s1,
  input  s2,
  input  s3,
  input  s4,
  input  s5,
  input  E,
  input  X,
  output O
);

  wire and_1_out, and_2_out, and_3_out, and_4_out, and_5_out, and_6_out, not_1_out, not_2_out, not_3_out,
       not_4_out, not_5_out;

  not not_1 (not_1_out, s1);
  not not_2 (not_2_out, s2);
  not not_3 (not_3_out, s3);
  not not_4 (not_4_out, s4);
  not not_5 (not_5_out, X);
  and and_1 (and_1_out, not_1_out, not_2_out, s3, s4, s5, X);
  and and_2 (and_2_out, not_1_out, s2, not_3_out, not_4_out, X);
  and and_3 (and_3_out, s1, s2, s3, s4, s5);
  and and_4 (and_4_out, s0, not_4_out, not_5_out);
  and and_5 (and_5_out, s0, s5);
  and and_6 (and_6_out, s0, s3, not_4_out);
  or or_1 (O, and_1_out, and_2_out, and_3_out, and_4_out, and_5_out, and_6_out);
endmodule

module s1_Circuit (
  input  s0,
  input  s1,
  input  s2,
  input  s3,
  input  s4,
  input  s5,
  input  E,
  input  X,
  output O
);

  wire and_1_out, and_2_out, and_3_out, and_4_out, and_5_out, and_6_out, and_7_out, and_8_out, and_9_out,
       not_1_out, not_2_out, not_3_out, not_4_out, not_5_out, not_6_out, not_7_out;

  not not_1 (not_1_out, s0);
  not not_2 (not_2_out, s1);
  not not_3 (not_3_out, s2);
  not not_4 (not_4_out, s3);
  not not_5 (not_5_out, s4);
  not not_6 (not_6_out, s5);
  not not_7 (not_7_out, X);
  and and_1 (and_1_out, not_1_out, not_3_out, not_4_out, s4, s5, X);
  and and_2 (and_2_out, not_1_out, not_2_out, not_3_out, s3, not_6_out, X);
  and and_3 (and_3_out, not_1_out, not_3_out, s3, not_5_out, X);
  and and_4 (and_4_out, not_2_out, s2, s3, s5, X);
  and and_5 (and_5_out, s1, not_5_out, not_7_out);
  and and_6 (and_6_out, s1, not_3_out, s5);
  and and_7 (and_7_out, s1, not_4_out, s5);
  and and_8 (and_8_out, s1, s2, not_5_out);
  and and_9 (and_9_out, s0, not_3_out, not_4_out, not_5_out, X);
  or or_1 (O, and_1_out, and_2_out, and_3_out, and_4_out, and_5_out, and_6_out, and_7_out, and_8_out, and_9_out);
endmodule

module s2_Circuit (
  input  s0,
  input  s1,
  input  s2,
  input  s3,
  input  s4,
  input  s5,
  input  E,
  input  X,
  output O
);

  wire and_1_out, and_2_out, and_3_out, and_4_out, and_5_out, and_6_out, and_7_out, and_8_out, and_9_out,
       and_10_out, and_11_out, and_12_out, and_13_out, and_14_out, not_1_out, not_2_out, not_3_out,
       not_4_out, not_5_out, not_6_out, not_7_out;

  not not_1 (not_1_out, s0);
  not not_2 (not_2_out, s1);
  not not_3 (not_3_out, s2);
  not not_4 (not_4_out, s3);
  not not_5 (not_5_out, s4);
  not not_6 (not_6_out, s5);
  not not_7 (not_7_out, X);
  and and_1 (and_1_out, not_5_out, s5, X);
  and and_2 (and_2_out, not_1_out, not_2_out, not_3_out, s4, not_6_out, X);
  and and_3 (and_3_out, s3, s4, s5, E, not_7_out);
  and and_4 (and_4_out, s2, not_5_out, not_7_out);
  and and_5 (and_5_out, s2, not_4_out, s5);
  and and_6 (and_6_out, s2, s5, not_7_out);
  and and_7 (and_7_out, s2, s3, not_5_out);
  and and_8 (and_8_out, s1, not_3_out, not_4_out, not_5_out, X);
  and and_9 (and_9_out, s1, not_3_out, s3, s5, X);
  and and_10 (and_10_out, s0, not_3_out, not_4_out, not_5_out, X);
  and and_11 (and_11_out, s0, s3, s5, X);
  and and_12 (and_12_out, s0, s3, s4, E);
  and and_13 (and_13_out, s0, s2, not_7_out);
  and and_14 (and_14_out, s0, s2, s4);
  or or_1 (O, and_1_out, and_2_out, and_3_out, and_4_out, and_5_out, and_6_out, and_7_out, and_8_out, and_9_out, and_10_out, and_11_out, and_12_out, and_13_out, and_14_out);
endmodule

module s3_Circuit (
  input  s0,
  input  s1,
  input  s2,
  input  s3,
  input  s4,
  input  s5,
  input  E,
  input  X,
  output O
);

  wire and_1_out, and_2_out, and_3_out, and_4_out, and_5_out, and_6_out, and_7_out, and_8_out, and_9_out,
       and_10_out, and_11_out, and_12_out, and_13_out, and_14_out, and_15_out, not_1_out, not_2_out,
       not_3_out, not_4_out, not_5_out, not_6_out, not_7_out, not_8_out;

  not not_1 (not_1_out, s0);
  not not_2 (not_2_out, s1);
  not not_3 (not_3_out, s2);
  not not_4 (not_4_out, s3);
  not not_5 (not_5_out, s4);
  not not_6 (not_6_out, s5);
  not not_7 (not_7_out, E);
  not not_8 (not_8_out, X);
  and and_1 (and_1_out, not_1_out, not_2_out, not_3_out, s4, X);
  and and_2 (and_2_out, not_4_out, s4, s5, E, not_8_out);
  and and_3 (and_3_out, not_1_out, not_2_out, not_3_out, s3, not_6_out);
  and and_4 (and_4_out, s3, not_5_out, not_8_out);
  and and_5 (and_5_out, s3, s5, not_7_out, not_8_out);
  and and_6 (and_6_out, not_1_out, not_3_out, s3, s4, not_6_out, E);
  and and_7 (and_7_out, s2, not_4_out, not_5_out, not_6_out, X);
  and and_8 (and_8_out, s2, not_4_out, s4, s5);
  and and_9 (and_9_out, s1, not_4_out, not_5_out, X);
  and and_10 (and_10_out, s1, not_4_out, s5, X);
  and and_11 (and_11_out, s1, s2, s4, not_6_out);
  and and_12 (and_12_out, s0, not_3_out, not_4_out, X);
  and and_13 (and_13_out, s0, not_3_out, not_4_out, s4);
  and and_14 (and_14_out, s0, not_3_out, s4, not_6_out, not_7_out);
  and and_15 (and_15_out, s0, not_3_out, s4, not_7_out, not_8_out);
  or or_1 (O, and_1_out, and_2_out, and_3_out, and_4_out, and_5_out, and_6_out, and_7_out, and_8_out, and_9_out, and_10_out, and_11_out, and_12_out, and_13_out, and_14_out, and_15_out);
endmodule

module s4_Circuit (
  input  s0,
  input  s1,
  input  s2,
  input  s3,
  input  s4,
  input  s5,
  input  E,
  input  X,
  output O
);

  wire and_1_out, and_2_out, and_3_out, and_4_out, and_5_out, and_6_out, and_7_out, and_8_out, and_9_out,
       and_10_out, and_11_out, and_12_out, and_13_out, and_14_out, and_15_out, and_16_out, and_17_out,
       not_1_out, not_2_out, not_3_out, not_4_out, not_5_out, not_6_out, not_7_out, not_8_out;

  not not_1 (not_1_out, s0);
  not not_2 (not_2_out, s1);
  not not_3 (not_3_out, s2);
  not not_4 (not_4_out, s3);
  not not_5 (not_5_out, s4);
  not not_6 (not_6_out, s5);
  not not_7 (not_7_out, E);
  not not_8 (not_8_out, X);
  and and_1 (and_1_out, not_1_out, not_2_out, not_3_out, s5, X);
  and and_2 (and_2_out, not_3_out, not_5_out, s5, E);
  and and_3 (and_3_out, not_1_out, not_2_out, not_3_out, s4, not_6_out);
  and and_4 (and_4_out, not_1_out, not_2_out, not_4_out, s4, not_7_out, not_8_out);
  and and_5 (and_5_out, not_3_out, s4, not_6_out, not_7_out);
  and and_6 (and_6_out, not_1_out, not_2_out, not_3_out, s4, X);
  and and_7 (and_7_out, s4, s5, not_7_out, not_8_out);
  and and_8 (and_8_out, not_1_out, not_2_out, not_3_out, s3, X);
  and and_9 (and_9_out, not_1_out, not_2_out, s3, E, X);
  and and_10 (and_10_out, s3, not_5_out, s5, E);
  and and_11 (and_11_out, not_1_out, not_2_out, s3, s4, not_6_out, E);
  and and_12 (and_12_out, not_1_out, not_2_out, s2, not_5_out, X);
  and and_13 (and_13_out, s2, s3, s4, E);
  and and_14 (and_14_out, s1, s5, E);
  and and_15 (and_15_out, s1, not_3_out, not_4_out, s4, E);
  and and_16 (and_16_out, s0, s5, E);
  and and_17 (and_17_out, s0, not_3_out, not_4_out, s4, E);
  or or_1 (O, and_1_out, and_2_out, and_3_out, and_4_out, and_5_out, and_6_out, and_7_out, and_8_out, and_9_out, and_10_out, and_11_out, and_12_out, and_13_out, and_14_out, and_15_out, and_16_out, and_17_out);
endmodule

module s5_Circuit (
  input  s0,
  input  s1,
  input  s2,
  input  s3,
  input  s4,
  input  s5,
  input  E,
  input  X,
  output O
);

  wire and_1_out, and_2_out, and_3_out, and_4_out, and_5_out, and_6_out, and_7_out, and_8_out, and_9_out,
       and_10_out, and_11_out, and_12_out, and_13_out, and_14_out, and_15_out, not_1_out, not_2_out,
       not_3_out, not_4_out, not_5_out, not_6_out, not_7_out, not_8_out;

  not not_1 (not_1_out, s0);
  not not_2 (not_2_out, s1);
  not not_3 (not_3_out, s2);
  not not_4 (not_4_out, s3);
  not not_5 (not_5_out, s4);
  not not_6 (not_6_out, s5);
  not not_7 (not_7_out, E);
  not not_8 (not_8_out, X);
  and and_1 (and_1_out, not_1_out, not_2_out, not_3_out, not_6_out, E);
  and and_2 (and_2_out, not_4_out, not_6_out, E, not_8_out);
  and and_3 (and_3_out, not_5_out, not_6_out, E, not_8_out);
  and and_4 (and_4_out, s5, not_7_out, not_8_out);
  and and_5 (and_5_out, not_5_out, s5, X);
  and and_6 (and_6_out, not_1_out, not_2_out, not_3_out, s4, X);
  and and_7 (and_7_out, not_1_out, not_2_out, not_3_out, s3, X);
  and and_8 (and_8_out, s3, s4, not_6_out, not_7_out, X);
  and and_9 (and_9_out, not_1_out, not_2_out, s2, not_4_out, not_5_out, X);
  and and_10 (and_10_out, not_1_out, not_2_out, s2, not_4_out, not_5_out, s5);
  and and_11 (and_11_out, s2, s3, s4, not_7_out, not_8_out);
  and and_12 (and_12_out, s1, not_4_out, s4, E);
  and and_13 (and_13_out, s1, s3, s4, not_6_out, not_7_out);
  and and_14 (and_14_out, s0, not_4_out, s4, E);
  and and_15 (and_15_out, s0, s3, s4, not_6_out, not_7_out);
  or or_1 (O, and_1_out, and_2_out, and_3_out, and_4_out, and_5_out, and_6_out, and_7_out, and_8_out, and_9_out, and_10_out, and_11_out, and_12_out, and_13_out, and_14_out, and_15_out);
endmodule

module LE_0 (
  input  s0,
  input  s1,
  input  s2,
  input  s3,
  input  s4,
  input  s5,
  output O
);

  wire and_1_out, and_2_out, and_3_out, and_4_out, not_1_out, not_2_out, not_3_out, not_4_out, not_5_out;

  not not_1 (not_1_out, s0);
  not not_2 (not_2_out, s1);
  not not_3 (not_3_out, s3);
  not not_4 (not_4_out, s4);
  not not_5 (not_5_out, s5);
  and and_1 (and_1_out, not_1_out, not_2_out, s2, not_3_out, s4, not_5_out);
  and and_2 (and_2_out, s2, s3, not_4_out);
  and and_3 (and_3_out, s1, not_4_out);
  and and_4 (and_4_out, s0, not_4_out);
  or or_1 (O, and_1_out, and_2_out, and_3_out, and_4_out);
endmodule

module LE_1 (
  input  s0,
  input  s1,
  input  s2,
  input  s3,
  input  s4,
  input  s5,
  output O
);

  wire and_1_out, and_2_out, and_3_out;

  and and_1 (and_1_out, s2, s4, s5);
  and and_2 (and_2_out, s1, s4, s5);
  and and_3 (and_3_out, s0, s4, s5);
  or or_1 (O, and_1_out, and_2_out, and_3_out);
endmodule

module LX_0 (
  input  s0,
  input  s1,
  input  s2,
  input  s3,
  input  s4,
  input  s5,
  output O
);

  wire and_1_out, and_2_out, and_3_out, and_4_out, and_5_out, and_6_out, and_7_out, not_1_out, not_2_out,
       not_3_out, not_4_out, not_5_out;

  not not_1 (not_1_out, s0);
  not not_2 (not_2_out, s1);
  not not_3 (not_3_out, s2);
  not not_4 (not_4_out, s3);
  not not_5 (not_5_out, s4);
  and and_1 (and_1_out, not_1_out, not_2_out, not_3_out);
  and and_2 (and_2_out, not_1_out, not_2_out, not_4_out, not_5_out);
  and and_3 (and_3_out, not_1_out, not_2_out, not_4_out, s5);
  and and_4 (and_4_out, s4, s5);
  and and_5 (and_5_out, s3, s4);
  and and_6 (and_6_out, s1, s4);
  and and_7 (and_7_out, s0, s4);
  or or_1 (O, and_1_out, and_2_out, and_3_out, and_4_out, and_5_out, and_6_out, and_7_out);
endmodule

module LX_1 (
  input  s0,
  input  s1,
  input  s2,
  input  s3,
  input  s4,
  input  s5,
  output O
);

  wire and_1_out, and_2_out, and_3_out, and_4_out, not_1_out, not_2_out, not_3_out, not_4_out, not_5_out;

  not not_1 (not_1_out, s0);
  not not_2 (not_2_out, s1);
  not not_3 (not_3_out, s3);
  not not_4 (not_4_out, s4);
  not not_5 (not_5_out, s5);
  and and_1 (and_1_out, not_1_out, not_2_out, s2, not_3_out, s4, not_5_out);
  and and_2 (and_2_out, s2, s3, not_4_out, s5);
  and and_3 (and_3_out, s1, not_4_out, s5);
  and and_4 (and_4_out, s0, not_4_out, s5);
  or or_1 (O, and_1_out, and_2_out, and_3_out, and_4_out);
endmodule

module C_0 (
  input  s0,
  input  s1,
  input  s2,
  input  s3,
  input  s4,
  input  s5,
  output O
);

  wire and_1_out, and_2_out, and_3_out, not_1_out, not_2_out, not_3_out;

  not not_1 (not_1_out, s1);
  not not_2 (not_2_out, s3);
  not not_3 (not_3_out, s4);
  and and_1 (and_1_out, not_1_out, s2, not_2_out, not_3_out);
  and and_2 (and_2_out, s0, s3, s4, s5);
  and and_3 (and_3_out, s0, s2);
  or or_1 (O, and_1_out, and_2_out, and_3_out);
endmodule

module C_1 (
  input  s0,
  input  s1,
  input  s2,
  input  s3,
  input  s4,
  input  s5,
  output O
);

  wire and_1_out, and_2_out, and_3_out, and_4_out, and_5_out, and_6_out, not_1_out, not_2_out, not_3_out,
       not_4_out, not_5_out, not_6_out;

  not not_1 (not_1_out, s0);
  not not_2 (not_2_out, s1);
  not not_3 (not_3_out, s2);
  not not_4 (not_4_out, s3);
  not not_5 (not_5_out, s4);
  not not_6 (not_6_out, s5);
  and and_1 (and_1_out, not_1_out, not_2_out, not_3_out, s3);
  and and_2 (and_2_out, not_1_out, not_3_out, s3, s4, s5);
  and and_3 (and_3_out, s1, s2);
  and and_4 (and_4_out, s0, not_3_out, not_4_out);
  and and_5 (and_5_out, s0, not_3_out, not_6_out);
  and and_6 (and_6_out, s0, s3, not_5_out, s5);
  or or_1 (O, and_1_out, and_2_out, and_3_out, and_4_out, and_5_out, and_6_out);
endmodule

module C_2 (
  input  s0,
  input  s1,
  input  s2,
  input  s3,
  input  s4,
  input  s5,
  output O
);

  wire and_1_out, and_2_out, and_3_out, and_4_out, and_5_out, and_6_out, and_7_out, and_8_out, and_9_out,
       not_1_out, not_2_out, not_3_out, not_4_out, not_5_out, not_6_out;

  not not_1 (not_1_out, s0);
  not not_2 (not_2_out, s1);
  not not_3 (not_3_out, s2);
  not not_4 (not_4_out, s3);
  not not_5 (not_5_out, s4);
  not not_6 (not_6_out, s5);
  and and_1 (and_1_out, not_1_out, not_2_out, not_3_out, s4);
  and and_2 (and_2_out, not_3_out, s4, not_6_out);
  and and_3 (and_3_out, s2, s3, s4, s5);
  and and_4 (and_4_out, s1, not_3_out, not_4_out);
  and and_5 (and_5_out, s1, not_3_out, not_5_out);
  and and_6 (and_6_out, s1, not_3_out, not_6_out);
  and and_7 (and_7_out, s0, not_3_out, not_4_out);
  and and_8 (and_8_out, s0, not_3_out, not_5_out);
  and and_9 (and_9_out, s0, not_3_out, not_6_out);
  or or_1 (O, and_1_out, and_2_out, and_3_out, and_4_out, and_5_out, and_6_out, and_7_out, and_8_out, and_9_out);
endmodule

module C_3 (
  input  s0,
  input  s1,
  input  s2,
  input  s3,
  input  s4,
  input  s5,
  output O
);

  wire and_1_out, and_2_out, and_3_out, and_4_out, and_5_out, and_6_out, and_7_out, not_1_out, not_2_out,
       not_3_out, not_4_out, not_5_out, not_6_out;

  not not_1 (not_1_out, s0);
  not not_2 (not_2_out, s1);
  not not_3 (not_3_out, s2);
  not not_4 (not_4_out, s3);
  not not_5 (not_5_out, s4);
  not not_6 (not_6_out, s5);
  and and_1 (and_1_out, not_1_out, not_2_out, not_3_out, s5);
  and and_2 (and_2_out, not_1_out, not_2_out, not_5_out, s5);
  and and_3 (and_3_out, not_4_out, s4, s5);
  and and_4 (and_4_out, s3, not_5_out, s5);
  and and_5 (and_5_out, s2, s3, not_6_out);
  and and_6 (and_6_out, s1, s3, not_6_out);
  and and_7 (and_7_out, s0, s3, not_6_out);
  or or_1 (O, and_1_out, and_2_out, and_3_out, and_4_out, and_5_out, and_6_out, and_7_out);
endmodule

module LESelector (
  input  LE0,
  input  LE1,
  output Red,
  output Yellow,
  output Green
);

  and and_1 (Red, LE0, ~LE1);  // AND_Gate
  and and_2 (Yellow, ~LE0, LE1);  // AND_Gate
  nor nor_1 (Green, LE0, LE1);
endmodule

module LXSelector (
  input  LX0,
  input  LX1,
  output Red,
  output Yellow,
  output Green
);

  and and_1 (Red, LX0, ~LX1);  // AND_Gate
  and and_2 (Yellow, ~LX0, LX1);  // AND_Gate
  nor nor_1 (Green, LX0, LX1);
endmodule
